# Fritzing sketch connections (saved by Fritzing 1.0.2b)
breadboards: 3

parts:
  Part1 = Arduino Uno (Rev3) - ICSP
  Mod1 = ESP32 - CAM
  Mod2 = ESP32 - CAM
  M1 = RioRand LM2596
  SP1 = SPEAKER [package=pcb_mount_speaker]
  VCC2 = 4 x AAA Battery Mount
  L298N1 = L298N DC motor driver
  Part2 = INMP441
  Part3 = KY-037 High Sensitivity Sound Detection Module [package="Breakout board"]
  U3 = SWITCH-SPST-2 [package=switch-spst-vertical]
  Squix1 = OLED 0.96" 128x64 I2C SSD1306
  Part4 = Adafruit MAX98357A I2S 3W Class D Amplifier [part_number="Adafruit #3006"]
  U4 = ESP32-38PinWide [part_number=ESP32-38PinWide]
  M3 = gear-motor
  M4 = gear-motor
  M2 = Dagu DGServo 9g (Top view) [part_number=RS001B]
  U2 = SWITCH-SPST-2 [package=switch-spst-vertical]
  M5 = RioRand LM2596
  JACK1 = 2.1mm Barrel Jack with Terminal Block
  M6 = Dagu DGServo 9g (Top view) [part_number=RS001B]
  U5 = LIPO-2000mAh [package=lipo-2000]
  U6 = LIPO-2000mAh [package=lipo-2000]

nets:
  N1: Part1.A0, M6.pulse
  N2: Part1.A4/SDA, Squix1.SCA
  N3: Part1.A5/SCL, Squix1.SCL
  N4: Part1.D8, L298N1.IN1
  N5: Part1.D9_PWM, M2.pulse
  GND: Part1.GND, M1.Pin_2, M1.Pin_4, L298N1.GND, Part2.GND, Part3.G, Squix1.GND, Part4.GND, U4.GND, U4.GPIO11, M2.gnd, M5.Pin_2, M5.Pin_4, JACK1.NEG, M6.gnd, U5.-
  N6: Part1.D0/RX, U4.GPIO13
  N7: Part1.D3_PWM, L298N1.ENB
  N8: Part1.D4, L298N1.IN4
  N9: Part1.D5_PWM, L298N1.IN3
  N10: Part1.D6_PWM, L298N1.ENA
  N11: Part1.D7, L298N1.IN2
  5V: Mod1.5V, Mod2.5V, U2.P
  GND_2: Mod1.GND, Mod2.GND, VCC2.-
  N12: M1.Pin_1, L298N1.12V, U3.O, JACK1.POS
  VCC: M1.Pin_3, Part3.+, Squix1.VCC, U4.VIN, M2.vcc, M5.Pin_1, M6.vcc
  N13: SP1.+, Part4.VO-
  N14: SP1.-, Part4.VO+
  N15: VCC2.+, U2.O
  N16: L298N1.OUT1, M3.pin_1
  N17: L298N1.OUT2, M3.pin_2
  N18: L298N1.OUT3, M4.pin_2
  N19: L298N1.OUT4, M4.pin_1
  N20: Part2.WS, U4.GPIO19
  N21: Part2.SCK, U4.GPIO18
  N22: Part2.SD, U4.GPIO26
  N23: Part2.VDD, M5.Pin_3
  N24: Part3.D0, U4.GPIO15
  N25: U3.P, U6.+
  N26: Part4.VIN, Part4.GAIN
  N27: Part4.SD_MODE, U4.GPIO21
  N28: Part4.DIN, U4.GPIO25
  N29: Part4.BCLK, U4.GPIO14
  N30: Part4.LRCLK, U4.GPIO12
  N31: U5.+, U6.-

notes:
  DC Gear Motor
  2x3.7 V Batteries
  400-Pin Breadboard
  2-Pin Switch
  L298N Motor Driver
  4x1.2V Batteries
  8 Ohm Speaker
  ESP32-WROVER
  KY-037 microphone
  INMP441 microphone
  Buck converter (7.4V to 5V)
  Arduino Uno
  SG-90 Servo
  170-Pin Breadboard
  MAX98357A Amplifier
  ESP32-CAM
  Buck converter (5V to 3.3V)
  OLED 128x64 SSD1306 Screen
  Possible improvements:
  - The cameras have a separate circuit. But the same 7.4 (down to 5)V battery could be used, provided it has enough mAh. Make sure voltage spikes are handled when servos or motors are used, though, or the drop could restart the cameras.
  - KY-037 (for sound detection, to trigger the recording) + INMP441 (to record) can probably be combined. For example, always listen and trigger upon wake word.
  - The motor driver is inefficient (but easy to use). You can look into DRV8833 if soldering is not a problem. 4 motors may provide better movement control than a rear caster wheel too.

custom parts:
  ESP32 - CAM: The ESP32-CAM has a very competitive small-size camera module that can operate independently as a minimum system with a footprint of only 27*40.5*4.5mm and a deep sleep current of up to 6mA.
  L298N DC motor driver: 2x DC motor driver with 78M05 positive voltage regulator (7..35 V) L298N: max 46 V, 2 A Set 5 V Enable jumper to enable 5 V regultor (needed for the L298N) and +5 V output at screw terminal or supply external +5 V at screw terminal Set ENA and/or ENB to +5 V to enable motor permanently or supply ENA and/or ENB with PWM signal IN1 and IN2 set rotation directory for motor A (OUT1/OUT2) IN2 and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
  INMP441: This is a simple breakout board for the INMP441 I2S MEMS microphone.
  KY-037 High Sensitivity Sound Detection Module: KY-037 high sensitivity sound detection module is an analog/digital sensor that uses a condenser microphone to observe changes in environment noise.
  Adafruit MAX98357A I2S 3W Class D Amplifier: Listen to this good news - we now have an all in one digital audio amp breakout board that works incredibly well with the Raspberry Pi! If you're looking for an easy and low cost way to get you digital sound files bumpin' then the MAX08357 I2S Amp Breakout is for you. It takes standard I2S digital audio input and, not only decodes it into analog, but also amplifies it directly into a speaker.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
  ESP32-38PinWide: Generic 38-Pin ESP32 with wide format (only access to one side of pins on a breadboard) based on Stephen Lilley's HiLetgo ESP-WROOM-32 ESP32 ESP-32S Development Board.
